# Fritzing sketch scorepref (saved by Fritzing 0.9.1b)
stripboards: 1

parts:
  Part1 = Arduino Pro Mini v13
  IC1 = ULN2003A [package="SO16 [SMD]"]
  R3 = Resistor [tolerance=±5% resistance=330 package=THT]
  R4 = Resistor [tolerance=±5% resistance=330 package=THT]
  R6 = Resistor [tolerance=±5% resistance=330 package=THT]
  R7 = Resistor [tolerance=±5% resistance=330 package=THT]
  R8 = Resistor [tolerance=±5% resistance=330 package=THT]
  R2 = Resistor [tolerance=±5% resistance=330 package=THT]
  J1 = female pin header, 5 pins [form="♀ (female)"]
  J2 = female pin header, 5 pins [form="♀ (female)"]
  R9 = Resistor [tolerance=±5% resistance=330 package=THT]
  R10 = Resistor [tolerance=±5% resistance=2.2k package=THT]
  R11 = Resistor [tolerance=±5% resistance=2.2k package=THT]
  12v_/_gnd = female pin header, 2 pins [form="♀ (female)"]
  Q1 = PNP-Transistor [package="SOT-23 [SMD]"]
  Q2 = PNP-Transistor [package="SOT-23 [SMD]"]
  J3 = female pin header, 5 pins [form="♀ (female)"]  # not connected
  J4 = female pin header, 5 pins [form="♀ (female)"]

nets:
  N1: Part1.RAW, 12v_/_gnd.pin2, Q1.2, Q2.2
  N2: Part1.GND, IC1.0V, 12v_/_gnd.pin1
  N3: Part1.D12/MISO, R11.Pin_1
  N4: Part1.D10_PWM/SS, R10.Pin_1
  N5: Part1.D9_PWM, IC1.In_1
  N6: Part1.D8, IC1.In_2
  N7: Part1.D7, IC1.In_3
  N8: Part1.D6_PWM, IC1.In_4
  N9: Part1.D5_PWM, IC1.In_5
  N10: Part1.D4, IC1.In_6
  N11: Part1.D3_PWM, IC1.In_7
  N12: IC1.Out_7, R9.Pin_0
  N13: IC1.Out_6, R6.Pin_0
  N14: IC1.Out_5, R8.Pin_0
  N15: IC1.Out_4, R7.Pin_1
  N16: IC1.Out_3, R4.Pin_0
  N17: IC1.Out_2, R3.Pin_0
  N18: IC1.Out_1, R2.Pin_0
  N19: R3.Pin_1, J2.pin3
  N20: R4.Pin_1, J2.pin4
  N21: R6.Pin_1, J1.pin4
  N22: R7.Pin_0, J1.pin1
  N23: R8.Pin_1, J1.pin2
  N24: R2.Pin_1, J2.pin2
  N25: J1.pin5, R9.Pin_1
  N26: J2.pin1, Q1.1
  N27: R10.Pin_0, Q1.0
  N28: R11.Pin_0, Q2.0
  N29: Q2.1, J4.pin1

notes:
  =diagram=
  56x37mm display
  A
  F B
  G
  E C
  D
  =pinout=
  10 9 8 7 6
  G F . A B
  + E D C +
  1 2 3 4 5
